# Fritzing sketch connection-diagram (saved by Fritzing 0.9.3b)

parts:
  Part1 = Arduino Uno (Rev3)
  S1 = Pushbutton [package="[THT]"]
  IR1 = TSOP312.., 314.. [package=THT]
  U2 = ENCODER_2LED [package=encoder_led_2]
  J3 = Camdenboss CTB0158-4 [part_number=CTB0158-4 package=THT]
  R1 = Resistor [tolerance=±5% resistance=330 package="2010 [SMD]"]

nets:
  N1: Part1.A3, IR1.Data
  N2: Part1.A4/SDA, IR1.Vs
  N3: Part1.A5/SCL, IR1.GND
  N4: Part1.D8, R1.Pin_0
  N5: Part1.GND, S1.Pin_1, J3.terminal_4
  N6: Part1.D2, S1.Pin_3, S1.Pin_4
  N7: Part1.D5_PWM, U2.SW
  N8: Part1.D6_PWM, U2.-
  N9: Part1.D7, U2.C
  N10: Part1.5V, J3.terminal_2
  N11: J3.terminal_3, R1.Pin_1

notes:
  Encoder
  Button
  IR Receiver
  NeoPixel
  Input Selector CS
  Attenuator CS
  Ground
  5V
  General Signal
  SPI SDI
  SPI CLK
  CLK
  SDI/ SI
  5V/VDD
  To attenutor and input selector PCBs
  }
